# Fritzing sketch Dust_Measurement_Network_Detector_Proto (saved by Fritzing 0.9.3b)
breadboards: 2

parts:
  Bauteil1 = Adafruit Feather M0 RFM9x LoRa [part_number="Adafruit #3178 or #3179"]
  Bauteil2 = VERTER 5V USB Buck-Boost
  AM1 = AM2302 Humidity and Temperature Sensor
  Bauteil3 = Adafruit 4-channel I2C-safe Bi-directional Logic Level Converter [part_number="Adafruit #757"]
  Bauteil4 = I2C Non-Volatile FRAM 32KB
  JP1 = Header 5 [package=1x05-1mm-ra]

nets:
  N1: Bauteil1.DIO1, Bauteil1.D6
  N2: Bauteil1.D1, Bauteil3.A1
  N3: Bauteil1.D0, Bauteil3.A2
  GND: Bauteil1.A4, Bauteil1.A3, Bauteil1.A2, Bauteil1.A1, Bauteil1.A0, Bauteil1.GND, Bauteil2.GND, AM1.GND, Bauteil3.GND, Bauteil4.GND, JP1.3
  +3V3: Bauteil1.+3V3, Bauteil2.VIN, AM1.VDD, Bauteil3.LV, Bauteil4.VCC
  N4: Bauteil1.D12, AM1.DATA
  N5: Bauteil1.SCL, Bauteil4.SCL
  N6: Bauteil1.SDA, Bauteil4.SDA
  N7: Bauteil2.5.0V, Bauteil3.HV, JP1.2
  N8: Bauteil3.B2, JP1.5
  N9: Bauteil3.B1, JP1.4

notes:
  SDS011: JST male header 5p in female housing (part to be changed)
  * RX (yellow)
  * TX (white)
  Issue #37 - GPIO 5-bit Device Serial Number
  - A0: Bit 0
  - A1: Bit 1
  - A2: Bit 2
  - A3: Bit 3
  - A4: Bit 4
  All 5 bits have an internal pull-up resistor, so open pins read in as high!
  Currently shown wiring enters 0 as Device Serial Number.

custom parts:
  Adafruit Feather M0 RFM9x LoRa: This is the Adafruit Feather M0 RFM95 LoRa Radio - our take on an microcontroller with a "Long Range (LoRa)" packet radio transceiver with built in USB and battery charging. Its an Adafruit Feather M0 with a 433Mhz or 900MHz radio module cooked in! Great for making wireless networks that are more flexible than Bluetooth LE and without the high power requirements of WiFi. We have other boards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
  VERTER 5V USB Buck-Boost: VERTER can take battery voltages from 3-12VDC and output a nice 5V DC, which makes it a perfect universal power supply for your portable project! Where Verter really shines is when you have a battery or power range that can fluctuate a lot, or you don't know what you'll end up using.
  Adafruit 4-channel I2C-safe Bi-directional Logic Level Converter: Because the Arduino (and Basic Stamp) are 5V devices, and most modern sensors, displays, flash cards and modes are 3.3V-only, many makers find that they need to perform level shifting/conversion to protect the 3.3V device from 5V. We do have some other handy level shifters in the shop, from the DIP 74LVC245 to the fancy bi-directional TXB0108. However, neither of these are happy to work with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
  I2C Non-Volatile FRAM 32KB: With our I2C FRAM breakout board you can add some FRAM storage to your next DIY project. FRAM allows for a lower power usage and a faster write performance. It's excellent for low-power or inconsistent-power datalogging or data buffering where you want to stream data fast while also keeping the data when there's no power. Unlike Flash or EEPROM there's no pages to worry about. Each byte can be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
